// Digital circuit 2-cpmpliment.dig as structural Verilog
module _2_cpmpliment (
  input  B0,
  input  B1,
  input  B2,
  input  B3,
  input  control,
  input  c,
  input  b,
  input  a,
  output S0,
  output S1,
  output S2,
  output S3
);

  wire xor_1_out, xor_2_out, xor_3_out, xor_4_out;

  xor xor_1 (xor_1_out, control, B3);
  xor xor_2 (xor_2_out, control, B2);
  xor xor_3 (xor_3_out, control, B1);
  xor xor_4 (xor_4_out, control, B0);
  _4bit_Add _4bit_add_1 (
    .A3(a), .A2(b), .A1(c), .A0(control), .B3(xor_1_out), .B2(xor_2_out), .B1(xor_3_out), .B0(xor_4_out),
    .S0(S0), .S1(S1), .S2(S2), .S3(S3));
endmodule
