// Digital circuit 4bit Add.dig as structural Verilog
module _4bit_Add (
  input  A3,
  input  A2,
  input  A1,
  input  A0,
  input  B3,
  input  B2,
  input  B1,
  input  B0,
  output S0,
  output S1,
  output S2,
  output S3
);

  wire FA_2_c_o, FA_3_c_o, HA_c0;

  Add FA (.a(A3), .b(B3), .c_i(FA_2_c_o), .s(S3));  // open: c_o
  Add FA_2 (.a(A2), .b(B2), .c_i(FA_3_c_o), .s(S2), .c_o(FA_2_c_o));
  Add FA_3 (.a(A1), .b(B1), .c_i(HA_c0), .s(S1), .c_o(FA_3_c_o));
  HA HA (.X(A0), .Y(B0), .S(S0), .C0(HA_c0));
endmodule
