// Digital circuit 4bit_add_minus.dig as structural Verilog
module _4bit_add_minus (
  input  [3:0] pin01,
  input  [3:0] pin02,
  input  control,
  input  _0,
  input  _0_2,
  input  _0_3,
  output [3:0] pout,
  output overflow
);

  wire _2_cpmpliment_1_s0, _2_cpmpliment_1_s1, _2_cpmpliment_1_s2, _2_cpmpliment_1_s3;

  _2_cpmpliment _2_cpmpliment_1 (
    .B0(pin02[0]), .B1(pin02[1]), .B2(pin02[2]), .B3(pin02[3]), .control(control), .c(_0), .b(_0_2),
    .a(_0_3), .S0(_2_cpmpliment_1_s0), .S1(_2_cpmpliment_1_s1), .S2(_2_cpmpliment_1_s2),
    .S3(_2_cpmpliment_1_s3));
  _4bit_Add_relay _4bit_add_relay_1 (
    .A3(pin01[3]), .B3(_2_cpmpliment_1_s3), .B2(_2_cpmpliment_1_s2), .A2(pin01[2]), .B1(_2_cpmpliment_1_s1),
    .A1(pin01[1]), .B0(_2_cpmpliment_1_s0), .A0(pin01[0]), .S0(pout[0]), .S1(pout[1]), .S2(pout[2]),
    .S3(pout[3]), .C3(overflow));
endmodule
