// Digital circuit 4bit Add_relay.dig as structural Verilog
module _4bit_Add_relay (
  input  A3,
  input  B3,
  input  B2,
  input  A2,
  input  B1,
  input  A1,
  input  B0,
  input  A0,
  output S0,
  output S1,
  output S2,
  output S3,
  output C3
);

  wire ha_1_c0, ha_2_c0, ha_2_s, ha_3_c0, ha_3_s, ha_4_c0, ha_4_s, ha_5_c0, ha_6_c0, ha_7_c0, or_1_out,
       or_2_out;

  HA ha_1 (.X(B0), .Y(A0), .S(S0), .C0(ha_1_c0));
  HA ha_2 (.X(B1), .Y(A1), .S(ha_2_s), .C0(ha_2_c0));
  HA ha_3 (.X(B2), .Y(A2), .S(ha_3_s), .C0(ha_3_c0));
  HA ha_4 (.X(B3), .Y(A3), .S(ha_4_s), .C0(ha_4_c0));
  HA ha_5 (.X(ha_1_c0), .Y(ha_2_s), .S(S1), .C0(ha_5_c0));
  HA ha_6 (.X(or_1_out), .Y(ha_3_s), .S(S2), .C0(ha_6_c0));
  HA ha_7 (.X(or_2_out), .Y(ha_4_s), .S(S3), .C0(ha_7_c0));
  or or_1 (or_1_out, ha_5_c0, ha_2_c0);
  or or_2 (or_2_out, ha_6_c0, ha_3_c0);
  or or_3 (C3, ha_7_c0, ha_4_c0);

  // Notes on the sheet:
  //   1 ketame
  //   4 ketame
  //   C...桁上げ出力
  //   S...和
  //   C0
  //   C1
  //   C2
endmodule
