// Digital circuit kadai2.dig as structural Verilog
module kadai2 (
  input  [3:0] pin01,
  input  [3:0] pin02,
  input  _0,
  output [7:0] pout
);

  wire _4bit_add_relay_1_c3, _4bit_add_relay_1_s1, _4bit_add_relay_1_s2, _4bit_add_relay_1_s3,
       _4bit_add_relay_2_c3, _4bit_add_relay_2_s1, _4bit_add_relay_2_s2, _4bit_add_relay_2_s3, and_2_out,
       and_3_out, and_4_out, and_5_out, and_6_out, and_7_out, and_8_out, and_9_out, and_10_out, and_11_out,
       and_12_out, and_13_out, and_14_out, and_15_out, and_16_out;

  and and_1 (pout[0], pin01[0], pin02[0]);
  and and_2 (and_2_out, pin01[1], pin02[0]);
  and and_3 (and_3_out, pin01[2], pin02[0]);
  and and_4 (and_4_out, pin01[3], pin02[0]);
  and and_5 (and_5_out, pin01[0], pin02[1]);
  and and_6 (and_6_out, pin01[1], pin02[1]);
  and and_7 (and_7_out, pin01[2], pin02[1]);
  and and_8 (and_8_out, pin01[3], pin02[1]);
  _4bit_Add_relay _4bit_add_relay_1 (
    .A3(_0), .B3(and_8_out), .B2(and_7_out), .A2(and_4_out), .B1(and_6_out), .A1(and_3_out), .B0(and_5_out),
    .A0(and_2_out), .S0(pout[1]), .S1(_4bit_add_relay_1_s1), .S2(_4bit_add_relay_1_s2),
    .S3(_4bit_add_relay_1_s3), .C3(_4bit_add_relay_1_c3));
  and and_9 (and_9_out, pin01[0], pin02[2]);
  and and_10 (and_10_out, pin01[1], pin02[2]);
  and and_11 (and_11_out, pin01[2], pin02[2]);
  and and_12 (and_12_out, pin01[3], pin02[2]);
  _4bit_Add_relay _4bit_add_relay_2 (
    .A3(_4bit_add_relay_1_c3), .B3(and_12_out), .B2(and_11_out), .A2(_4bit_add_relay_1_s3), .B1(and_10_out),
    .A1(_4bit_add_relay_1_s2), .B0(and_9_out), .A0(_4bit_add_relay_1_s1), .S0(pout[2]),
    .S1(_4bit_add_relay_2_s1), .S2(_4bit_add_relay_2_s2), .S3(_4bit_add_relay_2_s3), .C3(_4bit_add_relay_2_c3));
  and and_13 (and_13_out, pin01[0], pin02[3]);
  and and_14 (and_14_out, pin01[1], pin02[3]);
  and and_15 (and_15_out, pin01[2], pin02[3]);
  and and_16 (and_16_out, pin01[3], pin02[3]);
  _4bit_Add_relay _4bit_add_relay_3 (
    .A3(_4bit_add_relay_2_c3), .B3(and_16_out), .B2(and_15_out), .A2(_4bit_add_relay_2_s3), .B1(and_14_out),
    .A1(_4bit_add_relay_2_s2), .B0(and_13_out), .A0(_4bit_add_relay_2_s1), .S0(pout[3]), .S1(pout[4]),
    .S2(pout[5]), .S3(pout[6]), .C3(pout[7]));
endmodule
